// Logisim project aois-laba-4-1.circ as structural Verilog: 1 circuit, main circuit main
// 8
module main (
  input  [7:0] \Первое ,
  input  [7:0] \Второе ,
  input  [7:0] \Третье ,
  output out_4,
  output out_5,
  output out_6,
  output out_7,
  output \_7_бит ,
  output out_9,
  output out_10,
  output out_11,
  output out_12,
  output out_13,
  output \_6_бит ,
  output out_15,
  output out_16,
  output out_17,
  output out_18,
  output out_19,
  output \_5_бит ,
  output out_21,
  output [7:0] out_22,
  output out_23,
  output out_24,
  output out_25,
  output out_26,
  output \_4_бит ,
  output out_28,
  output out_29,
  output out_30,
  output out_31,
  output out_32,
  output \_3_бит ,
  output out_34,
  output out_35,
  output out_36,
  output out_37,
  output out_38,
  output \_2_бит ,
  output out_40,
  output out_41,
  output out_42,
  output out_43,
  output out_44,
  output \_1_бит ,
  output out_46,
  output out_47,
  output out_48,
  output \_0_бит ,
  output out_50,
  output out_51,
  output out_52,
  output out_53,
  output out_54,
  output \_7_бит_2 ,
  output out_56,
  output out_57,
  output out_58,
  output out_59,
  output out_60,
  output \_6_бит_2 ,
  output out_62,
  output out_63,
  output out_64,
  output out_65,
  output out_66,
  output \_5_бит_2 ,
  output out_68,
  output [7:0] out_69,
  output out_70,
  output out_71,
  output out_72,
  output out_73,
  output \_4_бит_2 ,
  output out_75,
  output out_76,
  output out_77,
  output out_78,
  output out_79,
  output \_3_бит_2 ,
  output out_81,
  output out_82,
  output out_83,
  output out_84,
  output out_85,
  output \_2_бит_2 ,
  output out_87,
  output out_88,
  output out_89,
  output out_90,
  output out_91,
  output \_1_бит_2 ,
  output out_93,
  output out_94,
  output out_95,
  output \_0_бит_2 ,
  output out_97
);

  wire and_40_out, and_42_out, and_44_out, and_46_out, and_48_out, and_50_out, and_52_out, and_54_out,
       and_56_out, and_58_out, and_60_out, and_62_out, not_1_out, not_2_out, not_3_out, not_4_out, not_5_out,
       not_6_out, not_7_out, not_8_out, not_9_out, not_10_out, not_11_out, not_12_out, not_13_out,
       not_14_out, not_15_out, not_16_out, not_17_out, not_18_out, not_19_out, not_20_out, not_21_out,
       not_22_out, not_23_out, not_24_out, not_25_out, not_26_out, not_27_out, not_28_out, not_29_out,
       not_30_out, not_31_out, not_32_out, not_33_out, not_34_out, not_35_out, not_36_out, not_37_out,
       not_38_out, not_39_out, not_40_out, not_41_out, not_42_out, not_43_out, not_44_out, not_45_out,
       not_46_out, not_47_out, not_48_out, not_49_out, not_50_out, not_51_out, not_52_out, not_53_out,
       not_54_out, not_55_out, not_56_out, not_57_out, not_58_out, not_59_out, not_60_out;

  // Probe on \Первое 
  // Probe on \Второе 
  // Probe on \Третье 
  not not_1 (not_1_out, \Третье [1]);
  not not_2 (not_2_out, \Второе [1]);
  not not_3 (not_3_out, \Третье [7]);
  not not_4 (not_4_out, \Третье [6]);
  not not_5 (not_5_out, \Третье [5]);
  not not_6 (not_6_out, \Третье [4]);
  not not_7 (not_7_out, \Третье [3]);
  not not_8 (not_8_out, \Третье [2]);
  not not_9 (not_9_out, \Третье [0]);
  not not_10 (not_10_out, \Второе [7]);
  not not_11 (not_11_out, \Второе [6]);
  not not_12 (not_12_out, \Второе [5]);
  not not_13 (not_13_out, \Второе [4]);
  not not_14 (not_14_out, \Второе [3]);
  not not_15 (not_15_out, \Второе [2]);
  not not_16 (not_16_out, \Второе [0]);
  not not_17 (not_17_out, \_1_бит );
  not not_18 (not_18_out, \_0_бит );
  not not_19 (not_19_out, \Первое [1]);
  not not_20 (not_20_out, \Первое [0]);
  not not_21 (not_21_out, \_7_бит );
  not not_22 (not_22_out, \_6_бит );
  not not_23 (not_23_out, \_5_бит );
  not not_24 (not_24_out, \_4_бит );
  not not_25 (not_25_out, \_3_бит );
  not not_26 (not_26_out, \_2_бит );
  and and_1 (out_88, not_17_out, \Третье [1]);
  and and_2 (out_91, \_1_бит , not_1_out);
  and and_3 (out_95, not_18_out, \Третье [0]);
  and and_4 (out_97, \_0_бит , not_9_out);
  not not_27 (not_27_out, \Первое [7]);
  not not_28 (not_28_out, \Первое [6]);
  not not_29 (not_29_out, \Первое [5]);
  not not_30 (not_30_out, \Первое [4]);
  not not_31 (not_31_out, \Первое [3]);
  not not_32 (not_32_out, \Первое [2]);
  and and_5 (out_41, not_19_out, \Второе [1]);
  and and_6 (out_44, \Первое [1], not_2_out);
  and and_7 (out_48, not_20_out, \Второе [0]);
  and and_8 (out_50, \Первое [0], not_16_out);
  and and_9 (out_51, not_21_out, \Третье [7]);
  and and_10 (out_54, \_7_бит , not_3_out);
  and and_11 (out_57, not_22_out, \Третье [6]);
  and and_12 (out_60, \_6_бит , not_4_out);
  and and_13 (out_63, not_23_out, \Третье [5]);
  and and_14 (out_66, \_5_бит , not_5_out);
  and and_15 (out_70, not_24_out, \Третье [4]);
  and and_16 (out_73, \_4_бит , not_6_out);
  and and_17 (out_76, not_25_out, \Третье [3]);
  and and_18 (out_79, \_3_бит , not_7_out);
  and and_19 (out_82, not_26_out, \Третье [2]);
  and and_20 (out_85, \_2_бит , not_8_out);
  and and_21 (out_4, not_27_out, \Второе [7]);
  and and_22 (out_7, \Первое [7], not_10_out);
  and and_23 (out_10, not_28_out, \Второе [6]);
  and and_24 (out_13, \Первое [6], not_11_out);
  and and_25 (out_16, not_29_out, \Второе [5]);
  and and_26 (out_19, \Первое [5], not_12_out);
  and and_27 (out_23, not_30_out, \Второе [4]);
  and and_28 (out_26, \Первое [4], not_13_out);
  and and_29 (out_29, not_31_out, \Второе [3]);
  and and_30 (out_32, \Первое [3], not_14_out);
  and and_31 (out_35, not_32_out, \Второе [2]);
  and and_32 (out_38, \Первое [2], not_15_out);
  or or_1 (out_90, out_88, out_91);
  and and_33 (out_94, 1'b1, 1'b1, out_95);
  or or_2 (\_0_бит_2 , out_95, out_97);
  or or_3 (out_43, out_41, out_44);
  and and_34 (out_47, 1'b1, 1'b1, out_48);
  or or_4 (\_0_бит , out_48, out_50);
  or or_5 (out_53, out_51, out_54);
  or or_6 (out_59, out_57, out_60);
  or or_7 (out_65, out_63, out_66);
  or or_8 (out_72, out_70, out_73);
  or or_9 (out_78, out_76, out_79);
  or or_10 (out_84, out_82, out_85);
  not not_33 (not_33_out, out_90);
  not not_34 (not_34_out, out_94);
  or or_11 (out_6, out_4, out_7);
  or or_12 (out_12, out_10, out_13);
  or or_13 (out_18, out_16, out_19);
  or or_14 (out_25, out_23, out_26);
  or or_15 (out_31, out_29, out_32);
  or or_16 (out_37, out_35, out_38);
  not not_35 (not_35_out, out_43);
  not not_36 (not_36_out, out_47);
  not not_37 (not_37_out, out_53);
  not not_38 (not_38_out, out_56);
  not not_39 (not_39_out, out_59);
  not not_40 (not_40_out, out_62);
  not not_41 (not_41_out, out_65);
  not not_42 (not_42_out, out_68);
  not not_43 (not_43_out, out_72);
  not not_44 (not_44_out, out_75);
  not not_45 (not_45_out, out_78);
  not not_46 (not_46_out, out_81);
  not not_47 (not_47_out, out_84);
  not not_48 (not_48_out, out_87);
  and and_35 (out_89, not_33_out, not_33_out, out_94);
  and and_36 (out_93, out_90, not_34_out);
  not not_49 (not_49_out, out_6);
  not not_50 (not_50_out, out_9);
  not not_51 (not_51_out, out_12);
  not not_52 (not_52_out, out_15);
  not not_53 (not_53_out, out_18);
  not not_54 (not_54_out, out_21);
  not not_55 (not_55_out, out_25);
  not not_56 (not_56_out, out_28);
  not not_57 (not_57_out, out_31);
  not not_58 (not_58_out, out_34);
  not not_59 (not_59_out, out_37);
  not not_60 (not_60_out, out_40);
  and and_37 (out_42, not_35_out, not_35_out, out_47);
  and and_38 (out_46, out_43, not_36_out);
  and and_39 (out_52, not_37_out, not_37_out, out_56);
  and and_40 (and_40_out, out_53, not_38_out);
  and and_41 (out_58, not_39_out, not_39_out, out_62);
  and and_42 (and_42_out, out_59, not_40_out);
  and and_43 (out_64, not_41_out, not_41_out, out_68);
  and and_44 (and_44_out, out_65, not_42_out);
  and and_45 (out_71, not_43_out, not_43_out, out_75);
  and and_46 (and_46_out, out_72, not_44_out);
  and and_47 (out_77, not_45_out, not_45_out, out_81);
  and and_48 (and_48_out, out_78, not_46_out);
  and and_49 (out_83, not_47_out, not_47_out, out_87);
  and and_50 (and_50_out, out_84, not_48_out);
  and and_51 (out_5, not_49_out, not_49_out, out_9);
  and and_52 (and_52_out, out_6, not_50_out);
  and and_53 (out_11, not_51_out, not_51_out, out_15);
  and and_54 (and_54_out, out_12, not_52_out);
  and and_55 (out_17, not_53_out, not_53_out, out_21);
  and and_56 (and_56_out, out_18, not_54_out);
  and and_57 (out_24, not_55_out, not_55_out, out_28);
  and and_58 (and_58_out, out_25, not_56_out);
  and and_59 (out_30, not_57_out, not_57_out, out_34);
  and and_60 (and_60_out, out_31, not_58_out);
  and and_61 (out_36, not_59_out, not_59_out, out_40);
  and and_62 (and_62_out, out_37, not_60_out);
  or or_17 (out_87, out_88, out_89);
  or or_18 (\_1_бит_2 , out_89, out_93);
  or or_19 (out_40, out_41, out_42);
  or or_20 (\_1_бит , out_42, out_46);
  or or_21 (\_7_бит_2 , out_52, and_40_out);
  or or_22 (out_56, out_57, out_58);
  or or_23 (\_6_бит_2 , out_58, and_42_out);
  or or_24 (out_62, out_63, out_64);
  or or_25 (\_5_бит_2 , out_64, and_44_out);
  or or_26 (out_68, out_70, out_71);
  or or_27 (\_4_бит_2 , out_71, and_46_out);
  or or_28 (out_75, out_76, out_77);
  or or_29 (\_3_бит_2 , out_77, and_48_out);
  or or_30 (out_81, out_82, out_83);
  or or_31 (\_2_бит_2 , out_83, and_50_out);
  or or_32 (\_7_бит , out_5, and_52_out);
  or or_33 (out_9, out_10, out_11);
  or or_34 (\_6_бит , out_11, and_54_out);
  or or_35 (out_15, out_16, out_17);
  or or_36 (\_5_бит , out_17, and_56_out);
  or or_37 (out_21, out_23, out_24);
  or or_38 (\_4_бит , out_24, and_58_out);
  or or_39 (out_28, out_29, out_30);
  or or_40 (\_3_бит , out_30, and_60_out);
  or or_41 (out_34, out_35, out_36);
  or or_42 (\_2_бит , out_36, and_62_out);
  // Probe on {\_7_бит_2 , \_6_бит_2 , \_5_бит_2 , \_4_бит_2 , \_3_бит_2 , \_2_бит_2 , \_1_бит_2 , \_0_бит_2 }
  // Probe on {\_7_бит , \_6_бит , \_5_бит , \_4_бит , \_3_бит , \_2_бит , \_1_бит , \_0_бит }

  assign out_22 = {\_7_бит , \_6_бит , \_5_бит , \_4_бит , \_3_бит , \_2_бит , \_1_бит , \_0_бит };
  assign out_69 = {\_7_бит_2 , \_6_бит_2 , \_5_бит_2 , \_4_бит_2 , \_3_бит_2 , \_2_бит_2 , \_1_бит_2 , \_0_бит_2 };

  // Other names for the same wires on the sheet: D0 = \_0_бит ; D1 = \_1_бит ; D2 = \_2_бит ; D3 = \_3_бит ;
  //   D4 = \_4_бит ; D5 = \_5_бит ; D6 = \_6_бит ; D7 = \_7_бит ; B0 = \Второе [0]; B1 = \Второе [1];
  //   B2 = \Второе [2]; B3 = \Второе [3]; B4 = \Второе [4]; B5 = \Второе [5]; B6 = \Второе [6]; B7 = \Второе [7];
  //   A0 = \Первое [0]; A1 = \Первое [1]; A2 = \Первое [2]; A3 = \Первое [3]; A4 = \Первое [4]; A5 = \Первое [5];
  //   A6 = \Первое [6]; A7 = \Первое [7]; C0 = \Третье [0]; C1 = \Третье [1]; C2 = \Третье [2]; C3 = \Третье [3];
  //   C4 = \Третье [4]; C5 = \Третье [5]; C6 = \Третье [6]; C7 = \Третье [7]
endmodule
