// Logisim project aois-laba-5.circ as structural Verilog: 1 circuit, main circuit main
// 8
module main (
  input  A,
  input  B,
  input  C,
  input  D,
  input  \Вход ,
  output out_6,
  output out_7,
  output out_8,
  output out_9,
  output out_10,
  output out_11,
  output out_12,
  output out_13
);

  wire and_5_out, and_6_out, and_7_out, and_8_out, and_9_out, and_10_out, and_11_out, and_12_out, not_1_out,
       not_2_out, not_3_out, not_4_out, not_5_out, not_6_out, not_7_out, not_8_out;

  // Probe on {A, B, C, D}
  and and_1 (out_7, B, C, D, \Вход );
  and and_2 (out_9, C, D, \Вход );
  and and_3 (out_11, D, \Вход );
  and and_4 (out_13, 1'b1, \Вход );
  // Probe on {out_7, out_9, out_11, out_13}
  not not_1 (not_1_out, A);
  and and_5 (and_5_out, not_1_out, out_7);
  and and_6 (and_6_out, A, not_2_out);
  not not_2 (not_2_out, out_7);
  not not_3 (not_3_out, B);
  and and_7 (and_7_out, not_3_out, out_9);
  and and_8 (and_8_out, B, not_4_out);
  not not_4 (not_4_out, out_9);
  not not_5 (not_5_out, C);
  and and_9 (and_9_out, not_5_out, out_11);
  and and_10 (and_10_out, C, not_6_out);
  not not_6 (not_6_out, out_11);
  not not_7 (not_7_out, D);
  and and_11 (and_11_out, not_7_out, out_13);
  and and_12 (and_12_out, D, not_8_out);
  not not_8 (not_8_out, out_13);
  or or_1 (out_6, and_5_out, and_6_out);
  or or_2 (out_8, and_7_out, and_8_out);
  or or_3 (out_10, and_9_out, and_10_out);
  or or_4 (out_12, and_11_out, and_12_out);
  // Probe on {out_6, out_8, out_10, out_12}

  // Notes on the sheet:
  //   a
  //   c
  //   b
  //   d
endmodule
